// Logisim project Multiplicador.circ as structural Verilog: 8 circuits, main circuit 32ANDs
module main (
  input  A31,
  input  B31,
  input  A30,
  input  A29,
  input  A28,
  input  A27,
  input  A26,
  input  A25,
  input  A24,
  input  A23,
  input  A22,
  input  A21,
  input  A20,
  input  A19,
  input  A18,
  input  A17,
  input  A16,
  input  A15,
  input  A14,
  input  A13,
  input  A12,
  input  A11,
  input  A10,
  input  A9,
  input  A8,
  input  A7,
  input  A6,
  input  A5,
  input  A4,
  input  A3,
  input  A2,
  input  A1,
  input  A0,
  input  B30,
  input  B29,
  input  B28,
  input  B27,
  input  B26,
  input  B25,
  input  B24,
  input  B23,
  input  B22,
  input  B21,
  input  B20,
  input  B19,
  input  B18,
  input  B17,
  input  B16,
  input  B15,
  input  B14,
  input  B13,
  input  B12,
  input  B11,
  input  B10,
  input  B9,
  input  B8,
  input  B7,
  input  B6,
  input  B5,
  input  B4,
  input  B3,
  input  B2,
  input  B1,
  input  B0,
  output S0,
  output S1,
  output S2,
  output S3,
  output S4,
  output S5,
  output S6,
  output S7,
  output S8,
  output S9,
  output S10,
  output S11,
  output S12,
  output S13,
  output S14,
  output S15,
  output S16,
  output S17,
  output S18,
  output S19,
  output S20,
  output S21,
  output S22,
  output S23,
  output S24,
  output S25,
  output S26,
  output S27,
  output S28,
  output S29,
  output S30,
  output S31
);

  wire soma_de_32_bits_1_cout, soma_de_32_bits_2_cout, soma_de_32_bits_3_cout, soma_de_32_bits_4_cout,
       soma_de_32_bits_5_cout, soma_de_32_bits_6_cout, soma_de_32_bits_7_cout, soma_de_32_bits_8_cout,
       soma_de_32_bits_9_cout, soma_de_32_bits_10_cout, soma_de_32_bits_11_cout, soma_de_32_bits_12_cout,
       soma_de_32_bits_13_cout, soma_de_32_bits_14_cout, soma_de_32_bits_15_cout, soma_de_32_bits_16_cout,
       soma_de_32_bits_17_cout, soma_de_32_bits_18_cout, soma_de_32_bits_19_cout, soma_de_32_bits_20_cout,
       soma_de_32_bits_21_cout, soma_de_32_bits_22_cout, soma_de_32_bits_23_cout, soma_de_32_bits_24_cout,
       soma_de_32_bits_25_cout, soma_de_32_bits_26_cout, soma_de_32_bits_27_cout, soma_de_32_bits_28_cout,
       soma_de_32_bits_29_cout, soma_de_32_bits_30_cout, soma_de_32_bits_31_cout;
  wire [31:0] n32ands_32_out_34, soma_de_32_bits_1_s, soma_de_32_bits_2_s, soma_de_32_bits_3_s,
       soma_de_32_bits_4_s, soma_de_32_bits_5_s, soma_de_32_bits_6_s, soma_de_32_bits_7_s,
       soma_de_32_bits_8_s, soma_de_32_bits_9_s, soma_de_32_bits_10_s, soma_de_32_bits_11_s,
       soma_de_32_bits_12_s, soma_de_32_bits_13_s, soma_de_32_bits_14_s, soma_de_32_bits_15_s,
       soma_de_32_bits_16_s, soma_de_32_bits_17_s, soma_de_32_bits_18_s, soma_de_32_bits_19_s,
       soma_de_32_bits_20_s, soma_de_32_bits_21_s, soma_de_32_bits_22_s, soma_de_32_bits_23_s,
       soma_de_32_bits_24_s, soma_de_32_bits_25_s, soma_de_32_bits_26_s, soma_de_32_bits_27_s,
       soma_de_32_bits_28_s, soma_de_32_bits_29_s, soma_de_32_bits_30_s;
  wire [31:1] n32ands_31_out_34;
  wire [31:2] n32ands_30_out_34;
  wire [31:3] n32ands_29_out_34;
  wire [31:4] n32ands_28_out_34;
  wire [31:5] n32ands_27_out_34;
  wire [31:6] n32ands_26_out_34;
  wire [31:7] n32ands_25_out_34;
  wire [31:8] n32ands_24_out_34;
  wire [31:9] n32ands_23_out_34;
  wire [31:10] n32ands_22_out_34;
  wire [31:11] n32ands_21_out_34;
  wire [31:12] n32ands_20_out_34;
  wire [31:13] n32ands_19_out_34;
  wire [31:14] n32ands_18_out_34;
  wire [31:15] n32ands_17_out_34;
  wire [31:16] n32ands_16_out_34;
  wire [31:17] n32ands_15_out_34;
  wire [31:18] n32ands_14_out_34;
  wire [31:19] n32ands_13_out_34;
  wire [31:20] n32ands_12_out_34;
  wire [31:21] n32ands_11_out_34;
  wire [31:22] n32ands_10_out_34;
  wire [31:23] n32ands_9_out_34;
  wire [31:24] n32ands_8_out_34;
  wire [31:25] n32ands_7_out_34;
  wire [31:26] n32ands_6_out_34;
  wire [31:27] n32ands_5_out_34;
  wire [31:28] n32ands_4_out_34;
  wire [31:29] n32ands_3_out_34;
  wire [31:30] n32ands_2_out_34;
  wire [31:31] n32ands_1_out_34, soma_de_32_bits_31_s;

  _32ANDs u_32ands_1 (
    .in_2(A0), .in_3(A1), .in_4(A2), .in_5(A3), .in_6(A4), .in_7(A5), .in_8(A6), .in_9(A7), .in_10(A8),
    .in_11(A9), .in_12(A10), .in_13(A11), .in_14(A12), .in_15(A13), .in_16(A14), .in_17(A15), .in_18(A16),
    .in_19(A17), .in_20(A18), .in_21(A19), .in_22(A20), .in_23(A21), .in_24(A22), .in_25(A23), .in_26(A24),
    .in_27(A25), .in_28(A26), .in_29(A27), .in_30(A28), .in_31(A29), .in_32(A30), .in_33(1'b0),
    .out_34(n32ands_1_out_34[31]), .in_1(1'b0));  // open: out_35, out_36, out_37, out_38, out_39, out_40, out_41, out_42, out_43, out_44, out_45, out_46, out_47, out_48, out_49, out_50, out_51, out_52, out_53, out_54, out_55, out_56, out_57, out_58, out_59, out_60, out_61, out_62, out_63, out_64, out_65
  _32ANDs u_32ands_2 (
    .in_2(A0), .in_3(A1), .in_4(A2), .in_5(A3), .in_6(A4), .in_7(A5), .in_8(A6), .in_9(A7), .in_10(A8),
    .in_11(A9), .in_12(A10), .in_13(A11), .in_14(A12), .in_15(A13), .in_16(A14), .in_17(A15), .in_18(A16),
    .in_19(A17), .in_20(A18), .in_21(A19), .in_22(A20), .in_23(A21), .in_24(A22), .in_25(A23), .in_26(A24),
    .in_27(A25), .in_28(A26), .in_29(A27), .in_30(A28), .in_31(A29), .in_32(A30), .in_33(1'b0),
    .out_34(n32ands_2_out_34[30]), .out_35(n32ands_2_out_34[31]), .in_1(B30));  // open: out_36, out_37, out_38, out_39, out_40, out_41, out_42, out_43, out_44, out_45, out_46, out_47, out_48, out_49, out_50, out_51, out_52, out_53, out_54, out_55, out_56, out_57, out_58, out_59, out_60, out_61, out_62, out_63, out_64, out_65
  _32ANDs u_32ands_3 (
    .in_2(A0), .in_3(A1), .in_4(A2), .in_5(A3), .in_6(A4), .in_7(A5), .in_8(A6), .in_9(A7), .in_10(A8),
    .in_11(A9), .in_12(A10), .in_13(A11), .in_14(A12), .in_15(A13), .in_16(A14), .in_17(A15), .in_18(A16),
    .in_19(A17), .in_20(A18), .in_21(A19), .in_22(A20), .in_23(A21), .in_24(A22), .in_25(A23), .in_26(A24),
    .in_27(A25), .in_28(A26), .in_29(A27), .in_30(A28), .in_31(A29), .in_32(A30), .in_33(1'b0),
    .out_34(n32ands_3_out_34[29]), .out_35(n32ands_3_out_34[30]), .out_36(n32ands_3_out_34[31]), .in_1(B29));  // open: out_37, out_38, out_39, out_40, out_41, out_42, out_43, out_44, out_45, out_46, out_47, out_48, out_49, out_50, out_51, out_52, out_53, out_54, out_55, out_56, out_57, out_58, out_59, out_60, out_61, out_62, out_63, out_64, out_65
  _32ANDs u_32ands_4 (
    .in_2(A0), .in_3(A1), .in_4(A2), .in_5(A3), .in_6(A4), .in_7(A5), .in_8(A6), .in_9(A7), .in_10(A8),
    .in_11(A9), .in_12(A10), .in_13(A11), .in_14(A12), .in_15(A13), .in_16(A14), .in_17(A15), .in_18(A16),
    .in_19(A17), .in_20(A18), .in_21(A19), .in_22(A20), .in_23(A21), .in_24(A22), .in_25(A23), .in_26(A24),
    .in_27(A25), .in_28(A26), .in_29(A27), .in_30(A28), .in_31(A29), .in_32(A30), .in_33(1'b0),
    .out_34(n32ands_4_out_34[28]), .out_35(n32ands_4_out_34[29]), .out_36(n32ands_4_out_34[30]),
    .out_37(n32ands_4_out_34[31]), .in_1(B28));  // open: out_38, out_39, out_40, out_41, out_42, out_43, out_44, out_45, out_46, out_47, out_48, out_49, out_50, out_51, out_52, out_53, out_54, out_55, out_56, out_57, out_58, out_59, out_60, out_61, out_62, out_63, out_64, out_65
  _32ANDs u_32ands_5 (
    .in_2(A0), .in_3(A1), .in_4(A2), .in_5(A3), .in_6(A4), .in_7(A5), .in_8(A6), .in_9(A7), .in_10(A8),
    .in_11(A9), .in_12(A10), .in_13(A11), .in_14(A12), .in_15(A13), .in_16(A14), .in_17(A15), .in_18(A16),
    .in_19(A17), .in_20(A18), .in_21(A19), .in_22(A20), .in_23(A21), .in_24(A22), .in_25(A23), .in_26(A24),
    .in_27(A25), .in_28(A26), .in_29(A27), .in_30(A28), .in_31(A29), .in_32(A30), .in_33(1'b0),
    .out_34(n32ands_5_out_34[27]), .out_35(n32ands_5_out_34[28]), .out_36(n32ands_5_out_34[29]),
    .out_37(n32ands_5_out_34[30]), .out_38(n32ands_5_out_34[31]), .in_1(B27));  // open: out_39, out_40, out_41, out_42, out_43, out_44, out_45, out_46, out_47, out_48, out_49, out_50, out_51, out_52, out_53, out_54, out_55, out_56, out_57, out_58, out_59, out_60, out_61, out_62, out_63, out_64, out_65
  _32ANDs u_32ands_6 (
    .in_2(A0), .in_3(A1), .in_4(A2), .in_5(A3), .in_6(A4), .in_7(A5), .in_8(A6), .in_9(A7), .in_10(A8),
    .in_11(A9), .in_12(A10), .in_13(A11), .in_14(A12), .in_15(A13), .in_16(A14), .in_17(A15), .in_18(A16),
    .in_19(A17), .in_20(A18), .in_21(A19), .in_22(A20), .in_23(A21), .in_24(A22), .in_25(A23), .in_26(A24),
    .in_27(A25), .in_28(A26), .in_29(A27), .in_30(A28), .in_31(A29), .in_32(A30), .in_33(1'b0),
    .out_34(n32ands_6_out_34[26]), .out_35(n32ands_6_out_34[27]), .out_36(n32ands_6_out_34[28]),
    .out_37(n32ands_6_out_34[29]), .out_38(n32ands_6_out_34[30]), .out_39(n32ands_6_out_34[31]), .in_1(B26));  // open: out_40, out_41, out_42, out_43, out_44, out_45, out_46, out_47, out_48, out_49, out_50, out_51, out_52, out_53, out_54, out_55, out_56, out_57, out_58, out_59, out_60, out_61, out_62, out_63, out_64, out_65
  _32ANDs u_32ands_7 (
    .in_2(A0), .in_3(A1), .in_4(A2), .in_5(A3), .in_6(A4), .in_7(A5), .in_8(A6), .in_9(A7), .in_10(A8),
    .in_11(A9), .in_12(A10), .in_13(A11), .in_14(A12), .in_15(A13), .in_16(A14), .in_17(A15), .in_18(A16),
    .in_19(A17), .in_20(A18), .in_21(A19), .in_22(A20), .in_23(A21), .in_24(A22), .in_25(A23), .in_26(A24),
    .in_27(A25), .in_28(A26), .in_29(A27), .in_30(A28), .in_31(A29), .in_32(A30), .in_33(1'b0),
    .out_34(n32ands_7_out_34[25]), .out_35(n32ands_7_out_34[26]), .out_36(n32ands_7_out_34[27]),
    .out_37(n32ands_7_out_34[28]), .out_38(n32ands_7_out_34[29]), .out_39(n32ands_7_out_34[30]),
    .out_40(n32ands_7_out_34[31]), .in_1(B25));  // open: out_41, out_42, out_43, out_44, out_45, out_46, out_47, out_48, out_49, out_50, out_51, out_52, out_53, out_54, out_55, out_56, out_57, out_58, out_59, out_60, out_61, out_62, out_63, out_64, out_65
  _32ANDs u_32ands_8 (
    .in_2(A0), .in_3(A1), .in_4(A2), .in_5(A3), .in_6(A4), .in_7(A5), .in_8(A6), .in_9(A7), .in_10(A8),
    .in_11(A9), .in_12(A10), .in_13(A11), .in_14(A12), .in_15(A13), .in_16(A14), .in_17(A15), .in_18(A16),
    .in_19(A17), .in_20(A18), .in_21(A19), .in_22(A20), .in_23(A21), .in_24(A22), .in_25(A23), .in_26(A24),
    .in_27(A25), .in_28(A26), .in_29(A27), .in_30(A28), .in_31(A29), .in_32(A30), .in_33(1'b0),
    .out_34(n32ands_8_out_34[24]), .out_35(n32ands_8_out_34[25]), .out_36(n32ands_8_out_34[26]),
    .out_37(n32ands_8_out_34[27]), .out_38(n32ands_8_out_34[28]), .out_39(n32ands_8_out_34[29]),
    .out_40(n32ands_8_out_34[30]), .out_41(n32ands_8_out_34[31]), .in_1(B24));  // open: out_42, out_43, out_44, out_45, out_46, out_47, out_48, out_49, out_50, out_51, out_52, out_53, out_54, out_55, out_56, out_57, out_58, out_59, out_60, out_61, out_62, out_63, out_64, out_65
  _32ANDs u_32ands_9 (
    .in_2(A0), .in_3(A1), .in_4(A2), .in_5(A3), .in_6(A4), .in_7(A5), .in_8(A6), .in_9(A7), .in_10(A8),
    .in_11(A9), .in_12(A10), .in_13(A11), .in_14(A12), .in_15(A13), .in_16(A14), .in_17(A15), .in_18(A16),
    .in_19(A17), .in_20(A18), .in_21(A19), .in_22(A20), .in_23(A21), .in_24(A22), .in_25(A23), .in_26(A24),
    .in_27(A25), .in_28(A26), .in_29(A27), .in_30(A28), .in_31(A29), .in_32(A30), .in_33(1'b0),
    .out_34(n32ands_9_out_34[23]), .out_35(n32ands_9_out_34[24]), .out_36(n32ands_9_out_34[25]),
    .out_37(n32ands_9_out_34[26]), .out_38(n32ands_9_out_34[27]), .out_39(n32ands_9_out_34[28]),
    .out_40(n32ands_9_out_34[29]), .out_41(n32ands_9_out_34[30]), .out_42(n32ands_9_out_34[31]), .in_1(B23));  // open: out_43, out_44, out_45, out_46, out_47, out_48, out_49, out_50, out_51, out_52, out_53, out_54, out_55, out_56, out_57, out_58, out_59, out_60, out_61, out_62, out_63, out_64, out_65
  _32ANDs u_32ands_10 (
    .in_2(A0), .in_3(A1), .in_4(A2), .in_5(A3), .in_6(A4), .in_7(A5), .in_8(A6), .in_9(A7), .in_10(A8),
    .in_11(A9), .in_12(A10), .in_13(A11), .in_14(A12), .in_15(A13), .in_16(A14), .in_17(A15), .in_18(A16),
    .in_19(A17), .in_20(A18), .in_21(A19), .in_22(A20), .in_23(A21), .in_24(A22), .in_25(A23), .in_26(A24),
    .in_27(A25), .in_28(A26), .in_29(A27), .in_30(A28), .in_31(A29), .in_32(A30), .in_33(1'b0),
    .out_34(n32ands_10_out_34[22]), .out_35(n32ands_10_out_34[23]), .out_36(n32ands_10_out_34[24]),
    .out_37(n32ands_10_out_34[25]), .out_38(n32ands_10_out_34[26]), .out_39(n32ands_10_out_34[27]),
    .out_40(n32ands_10_out_34[28]), .out_41(n32ands_10_out_34[29]), .out_42(n32ands_10_out_34[30]),
    .out_43(n32ands_10_out_34[31]), .in_1(B22));  // open: out_44, out_45, out_46, out_47, out_48, out_49, out_50, out_51, out_52, out_53, out_54, out_55, out_56, out_57, out_58, out_59, out_60, out_61, out_62, out_63, out_64, out_65
  _32ANDs u_32ands_11 (
    .in_2(A0), .in_3(A1), .in_4(A2), .in_5(A3), .in_6(A4), .in_7(A5), .in_8(A6), .in_9(A7), .in_10(A8),
    .in_11(A9), .in_12(A10), .in_13(A11), .in_14(A12), .in_15(A13), .in_16(A14), .in_17(A15), .in_18(A16),
    .in_19(A17), .in_20(A18), .in_21(A19), .in_22(A20), .in_23(A21), .in_24(A22), .in_25(A23), .in_26(A24),
    .in_27(A25), .in_28(A26), .in_29(A27), .in_30(A28), .in_31(A29), .in_32(A30), .in_33(1'b0),
    .out_34(n32ands_11_out_34[21]), .out_35(n32ands_11_out_34[22]), .out_36(n32ands_11_out_34[23]),
    .out_37(n32ands_11_out_34[24]), .out_38(n32ands_11_out_34[25]), .out_39(n32ands_11_out_34[26]),
    .out_40(n32ands_11_out_34[27]), .out_41(n32ands_11_out_34[28]), .out_42(n32ands_11_out_34[29]),
    .out_43(n32ands_11_out_34[30]), .out_44(n32ands_11_out_34[31]), .in_1(B21));  // open: out_45, out_46, out_47, out_48, out_49, out_50, out_51, out_52, out_53, out_54, out_55, out_56, out_57, out_58, out_59, out_60, out_61, out_62, out_63, out_64, out_65
  _32ANDs u_32ands_12 (
    .in_2(A0), .in_3(A1), .in_4(A2), .in_5(A3), .in_6(A4), .in_7(A5), .in_8(A6), .in_9(A7), .in_10(A8),
    .in_11(A9), .in_12(A10), .in_13(A11), .in_14(A12), .in_15(A13), .in_16(A14), .in_17(A15), .in_18(A16),
    .in_19(A17), .in_20(A18), .in_21(A19), .in_22(A20), .in_23(A21), .in_24(A22), .in_25(A23), .in_26(A24),
    .in_27(A25), .in_28(A26), .in_29(A27), .in_30(A28), .in_31(A29), .in_32(A30), .in_33(1'b0),
    .out_34(n32ands_12_out_34[20]), .out_35(n32ands_12_out_34[21]), .out_36(n32ands_12_out_34[22]),
    .out_37(n32ands_12_out_34[23]), .out_38(n32ands_12_out_34[24]), .out_39(n32ands_12_out_34[25]),
    .out_40(n32ands_12_out_34[26]), .out_41(n32ands_12_out_34[27]), .out_42(n32ands_12_out_34[28]),
    .out_43(n32ands_12_out_34[29]), .out_44(n32ands_12_out_34[30]), .out_45(n32ands_12_out_34[31]), .in_1(B20));  // open: out_46, out_47, out_48, out_49, out_50, out_51, out_52, out_53, out_54, out_55, out_56, out_57, out_58, out_59, out_60, out_61, out_62, out_63, out_64, out_65
  _32ANDs u_32ands_13 (
    .in_2(A0), .in_3(A1), .in_4(A2), .in_5(A3), .in_6(A4), .in_7(A5), .in_8(A6), .in_9(A7), .in_10(A8),
    .in_11(A9), .in_12(A10), .in_13(A11), .in_14(A12), .in_15(A13), .in_16(A14), .in_17(A15), .in_18(A16),
    .in_19(A17), .in_20(A18), .in_21(A19), .in_22(A20), .in_23(A21), .in_24(A22), .in_25(A23), .in_26(A24),
    .in_27(A25), .in_28(A26), .in_29(A27), .in_30(A28), .in_31(A29), .in_32(A30), .in_33(1'b0),
    .out_34(n32ands_13_out_34[19]), .out_35(n32ands_13_out_34[20]), .out_36(n32ands_13_out_34[21]),
    .out_37(n32ands_13_out_34[22]), .out_38(n32ands_13_out_34[23]), .out_39(n32ands_13_out_34[24]),
    .out_40(n32ands_13_out_34[25]), .out_41(n32ands_13_out_34[26]), .out_42(n32ands_13_out_34[27]),
    .out_43(n32ands_13_out_34[28]), .out_44(n32ands_13_out_34[29]), .out_45(n32ands_13_out_34[30]),
    .out_46(n32ands_13_out_34[31]), .in_1(B19));  // open: out_47, out_48, out_49, out_50, out_51, out_52, out_53, out_54, out_55, out_56, out_57, out_58, out_59, out_60, out_61, out_62, out_63, out_64, out_65
  _32ANDs u_32ands_14 (
    .in_2(A0), .in_3(A1), .in_4(A2), .in_5(A3), .in_6(A4), .in_7(A5), .in_8(A6), .in_9(A7), .in_10(A8),
    .in_11(A9), .in_12(A10), .in_13(A11), .in_14(A12), .in_15(A13), .in_16(A14), .in_17(A15), .in_18(A16),
    .in_19(A17), .in_20(A18), .in_21(A19), .in_22(A20), .in_23(A21), .in_24(A22), .in_25(A23), .in_26(A24),
    .in_27(A25), .in_28(A26), .in_29(A27), .in_30(A28), .in_31(A29), .in_32(A30), .in_33(1'b0),
    .out_34(n32ands_14_out_34[18]), .out_35(n32ands_14_out_34[19]), .out_36(n32ands_14_out_34[20]),
    .out_37(n32ands_14_out_34[21]), .out_38(n32ands_14_out_34[22]), .out_39(n32ands_14_out_34[23]),
    .out_40(n32ands_14_out_34[24]), .out_41(n32ands_14_out_34[25]), .out_42(n32ands_14_out_34[26]),
    .out_43(n32ands_14_out_34[27]), .out_44(n32ands_14_out_34[28]), .out_45(n32ands_14_out_34[29]),
    .out_46(n32ands_14_out_34[30]), .out_47(n32ands_14_out_34[31]), .in_1(B18));  // open: out_48, out_49, out_50, out_51, out_52, out_53, out_54, out_55, out_56, out_57, out_58, out_59, out_60, out_61, out_62, out_63, out_64, out_65
  _32ANDs u_32ands_15 (
    .in_2(A0), .in_3(A1), .in_4(A2), .in_5(A3), .in_6(A4), .in_7(A5), .in_8(A6), .in_9(A7), .in_10(A8),
    .in_11(A9), .in_12(A10), .in_13(A11), .in_14(A12), .in_15(A13), .in_16(A14), .in_17(A15), .in_18(A16),
    .in_19(A17), .in_20(A18), .in_21(A19), .in_22(A20), .in_23(A21), .in_24(A22), .in_25(A23), .in_26(A24),
    .in_27(A25), .in_28(A26), .in_29(A27), .in_30(A28), .in_31(A29), .in_32(A30), .in_33(1'b0),
    .out_34(n32ands_15_out_34[17]), .out_35(n32ands_15_out_34[18]), .out_36(n32ands_15_out_34[19]),
    .out_37(n32ands_15_out_34[20]), .out_38(n32ands_15_out_34[21]), .out_39(n32ands_15_out_34[22]),
    .out_40(n32ands_15_out_34[23]), .out_41(n32ands_15_out_34[24]), .out_42(n32ands_15_out_34[25]),
    .out_43(n32ands_15_out_34[26]), .out_44(n32ands_15_out_34[27]), .out_45(n32ands_15_out_34[28]),
    .out_46(n32ands_15_out_34[29]), .out_47(n32ands_15_out_34[30]), .out_48(n32ands_15_out_34[31]), .in_1(B17));  // open: out_49, out_50, out_51, out_52, out_53, out_54, out_55, out_56, out_57, out_58, out_59, out_60, out_61, out_62, out_63, out_64, out_65
  _32ANDs u_32ands_16 (
    .in_2(A0), .in_3(A1), .in_4(A2), .in_5(A3), .in_6(A4), .in_7(A5), .in_8(A6), .in_9(A7), .in_10(A8),
    .in_11(A9), .in_12(A10), .in_13(A11), .in_14(A12), .in_15(A13), .in_16(A14), .in_17(A15), .in_18(A16),
    .in_19(A17), .in_20(A18), .in_21(A19), .in_22(A20), .in_23(A21), .in_24(A22), .in_25(A23), .in_26(A24),
    .in_27(A25), .in_28(A26), .in_29(A27), .in_30(A28), .in_31(A29), .in_32(A30), .in_33(1'b0),
    .out_34(n32ands_16_out_34[16]), .out_35(n32ands_16_out_34[17]), .out_36(n32ands_16_out_34[18]),
    .out_37(n32ands_16_out_34[19]), .out_38(n32ands_16_out_34[20]), .out_39(n32ands_16_out_34[21]),
    .out_40(n32ands_16_out_34[22]), .out_41(n32ands_16_out_34[23]), .out_42(n32ands_16_out_34[24]),
    .out_43(n32ands_16_out_34[25]), .out_44(n32ands_16_out_34[26]), .out_45(n32ands_16_out_34[27]),
    .out_46(n32ands_16_out_34[28]), .out_47(n32ands_16_out_34[29]), .out_48(n32ands_16_out_34[30]),
    .out_49(n32ands_16_out_34[31]), .in_1(B16));  // open: out_50, out_51, out_52, out_53, out_54, out_55, out_56, out_57, out_58, out_59, out_60, out_61, out_62, out_63, out_64, out_65
  _32ANDs u_32ands_17 (
    .in_2(A0), .in_3(A1), .in_4(A2), .in_5(A3), .in_6(A4), .in_7(A5), .in_8(A6), .in_9(A7), .in_10(A8),
    .in_11(A9), .in_12(A10), .in_13(A11), .in_14(A12), .in_15(A13), .in_16(A14), .in_17(A15), .in_18(A16),
    .in_19(A17), .in_20(A18), .in_21(A19), .in_22(A20), .in_23(A21), .in_24(A22), .in_25(A23), .in_26(A24),
    .in_27(A25), .in_28(A26), .in_29(A27), .in_30(A28), .in_31(A29), .in_32(A30), .in_33(1'b0),
    .out_34(n32ands_17_out_34[15]), .out_35(n32ands_17_out_34[16]), .out_36(n32ands_17_out_34[17]),
    .out_37(n32ands_17_out_34[18]), .out_38(n32ands_17_out_34[19]), .out_39(n32ands_17_out_34[20]),
    .out_40(n32ands_17_out_34[21]), .out_41(n32ands_17_out_34[22]), .out_42(n32ands_17_out_34[23]),
    .out_43(n32ands_17_out_34[24]), .out_44(n32ands_17_out_34[25]), .out_45(n32ands_17_out_34[26]),
    .out_46(n32ands_17_out_34[27]), .out_47(n32ands_17_out_34[28]), .out_48(n32ands_17_out_34[29]),
    .out_49(n32ands_17_out_34[30]), .out_50(n32ands_17_out_34[31]), .in_1(B15));  // open: out_51, out_52, out_53, out_54, out_55, out_56, out_57, out_58, out_59, out_60, out_61, out_62, out_63, out_64, out_65
  _32ANDs u_32ands_18 (
    .in_2(A0), .in_3(A1), .in_4(A2), .in_5(A3), .in_6(A4), .in_7(A5), .in_8(A6), .in_9(A7), .in_10(A8),
    .in_11(A9), .in_12(A10), .in_13(A11), .in_14(A12), .in_15(A13), .in_16(A14), .in_17(A15), .in_18(A16),
    .in_19(A17), .in_20(A18), .in_21(A19), .in_22(A20), .in_23(A21), .in_24(A22), .in_25(A23), .in_26(A24),
    .in_27(A25), .in_28(A26), .in_29(A27), .in_30(A28), .in_31(A29), .in_32(A30), .in_33(1'b0),
    .out_34(n32ands_18_out_34[14]), .out_35(n32ands_18_out_34[15]), .out_36(n32ands_18_out_34[16]),
    .out_37(n32ands_18_out_34[17]), .out_38(n32ands_18_out_34[18]), .out_39(n32ands_18_out_34[19]),
    .out_40(n32ands_18_out_34[20]), .out_41(n32ands_18_out_34[21]), .out_42(n32ands_18_out_34[22]),
    .out_43(n32ands_18_out_34[23]), .out_44(n32ands_18_out_34[24]), .out_45(n32ands_18_out_34[25]),
    .out_46(n32ands_18_out_34[26]), .out_47(n32ands_18_out_34[27]), .out_48(n32ands_18_out_34[28]),
    .out_49(n32ands_18_out_34[29]), .out_50(n32ands_18_out_34[30]), .out_51(n32ands_18_out_34[31]), .in_1(B14));  // open: out_52, out_53, out_54, out_55, out_56, out_57, out_58, out_59, out_60, out_61, out_62, out_63, out_64, out_65
  _32ANDs u_32ands_19 (
    .in_2(A0), .in_3(A1), .in_4(A2), .in_5(A3), .in_6(A4), .in_7(A5), .in_8(A6), .in_9(A7), .in_10(A8),
    .in_11(A9), .in_12(A10), .in_13(A11), .in_14(A12), .in_15(A13), .in_16(A14), .in_17(A15), .in_18(A16),
    .in_19(A17), .in_20(A18), .in_21(A19), .in_22(A20), .in_23(A21), .in_24(A22), .in_25(A23), .in_26(A24),
    .in_27(A25), .in_28(A26), .in_29(A27), .in_30(A28), .in_31(A29), .in_32(A30), .in_33(1'b0),
    .out_34(n32ands_19_out_34[13]), .out_35(n32ands_19_out_34[14]), .out_36(n32ands_19_out_34[15]),
    .out_37(n32ands_19_out_34[16]), .out_38(n32ands_19_out_34[17]), .out_39(n32ands_19_out_34[18]),
    .out_40(n32ands_19_out_34[19]), .out_41(n32ands_19_out_34[20]), .out_42(n32ands_19_out_34[21]),
    .out_43(n32ands_19_out_34[22]), .out_44(n32ands_19_out_34[23]), .out_45(n32ands_19_out_34[24]),
    .out_46(n32ands_19_out_34[25]), .out_47(n32ands_19_out_34[26]), .out_48(n32ands_19_out_34[27]),
    .out_49(n32ands_19_out_34[28]), .out_50(n32ands_19_out_34[29]), .out_51(n32ands_19_out_34[30]),
    .out_52(n32ands_19_out_34[31]), .in_1(B13));  // open: out_53, out_54, out_55, out_56, out_57, out_58, out_59, out_60, out_61, out_62, out_63, out_64, out_65
  _32ANDs u_32ands_20 (
    .in_2(A0), .in_3(A1), .in_4(A2), .in_5(A3), .in_6(A4), .in_7(A5), .in_8(A6), .in_9(A7), .in_10(A8),
    .in_11(A9), .in_12(A10), .in_13(A11), .in_14(A12), .in_15(A13), .in_16(A14), .in_17(A15), .in_18(A16),
    .in_19(A17), .in_20(A18), .in_21(A19), .in_22(A20), .in_23(A21), .in_24(A22), .in_25(A23), .in_26(A24),
    .in_27(A25), .in_28(A26), .in_29(A27), .in_30(A28), .in_31(A29), .in_32(A30), .in_33(1'b0),
    .out_34(n32ands_20_out_34[12]), .out_35(n32ands_20_out_34[13]), .out_36(n32ands_20_out_34[14]),
    .out_37(n32ands_20_out_34[15]), .out_38(n32ands_20_out_34[16]), .out_39(n32ands_20_out_34[17]),
    .out_40(n32ands_20_out_34[18]), .out_41(n32ands_20_out_34[19]), .out_42(n32ands_20_out_34[20]),
    .out_43(n32ands_20_out_34[21]), .out_44(n32ands_20_out_34[22]), .out_45(n32ands_20_out_34[23]),
    .out_46(n32ands_20_out_34[24]), .out_47(n32ands_20_out_34[25]), .out_48(n32ands_20_out_34[26]),
    .out_49(n32ands_20_out_34[27]), .out_50(n32ands_20_out_34[28]), .out_51(n32ands_20_out_34[29]),
    .out_52(n32ands_20_out_34[30]), .out_53(n32ands_20_out_34[31]), .in_1(B12));  // open: out_54, out_55, out_56, out_57, out_58, out_59, out_60, out_61, out_62, out_63, out_64, out_65
  _32ANDs u_32ands_21 (
    .in_2(A0), .in_3(A1), .in_4(A2), .in_5(A3), .in_6(A4), .in_7(A5), .in_8(A6), .in_9(A7), .in_10(A8),
    .in_11(A9), .in_12(A10), .in_13(A11), .in_14(A12), .in_15(A13), .in_16(A14), .in_17(A15), .in_18(A16),
    .in_19(A17), .in_20(A18), .in_21(A19), .in_22(A20), .in_23(A21), .in_24(A22), .in_25(A23), .in_26(A24),
    .in_27(A25), .in_28(A26), .in_29(A27), .in_30(A28), .in_31(A29), .in_32(A30), .in_33(1'b0),
    .out_34(n32ands_21_out_34[11]), .out_35(n32ands_21_out_34[12]), .out_36(n32ands_21_out_34[13]),
    .out_37(n32ands_21_out_34[14]), .out_38(n32ands_21_out_34[15]), .out_39(n32ands_21_out_34[16]),
    .out_40(n32ands_21_out_34[17]), .out_41(n32ands_21_out_34[18]), .out_42(n32ands_21_out_34[19]),
    .out_43(n32ands_21_out_34[20]), .out_44(n32ands_21_out_34[21]), .out_45(n32ands_21_out_34[22]),
    .out_46(n32ands_21_out_34[23]), .out_47(n32ands_21_out_34[24]), .out_48(n32ands_21_out_34[25]),
    .out_49(n32ands_21_out_34[26]), .out_50(n32ands_21_out_34[27]), .out_51(n32ands_21_out_34[28]),
    .out_52(n32ands_21_out_34[29]), .out_53(n32ands_21_out_34[30]), .out_54(n32ands_21_out_34[31]), .in_1(B11));  // open: out_55, out_56, out_57, out_58, out_59, out_60, out_61, out_62, out_63, out_64, out_65
  _32ANDs u_32ands_22 (
    .in_2(A0), .in_3(A1), .in_4(A2), .in_5(A3), .in_6(A4), .in_7(A5), .in_8(A6), .in_9(A7), .in_10(A8),
    .in_11(A9), .in_12(A10), .in_13(A11), .in_14(A12), .in_15(A13), .in_16(A14), .in_17(A15), .in_18(A16),
    .in_19(A17), .in_20(A18), .in_21(A19), .in_22(A20), .in_23(A21), .in_24(A22), .in_25(A23), .in_26(A24),
    .in_27(A25), .in_28(A26), .in_29(A27), .in_30(A28), .in_31(A29), .in_32(A30), .in_33(1'b0),
    .out_34(n32ands_22_out_34[10]), .out_35(n32ands_22_out_34[11]), .out_36(n32ands_22_out_34[12]),
    .out_37(n32ands_22_out_34[13]), .out_38(n32ands_22_out_34[14]), .out_39(n32ands_22_out_34[15]),
    .out_40(n32ands_22_out_34[16]), .out_41(n32ands_22_out_34[17]), .out_42(n32ands_22_out_34[18]),
    .out_43(n32ands_22_out_34[19]), .out_44(n32ands_22_out_34[20]), .out_45(n32ands_22_out_34[21]),
    .out_46(n32ands_22_out_34[22]), .out_47(n32ands_22_out_34[23]), .out_48(n32ands_22_out_34[24]),
    .out_49(n32ands_22_out_34[25]), .out_50(n32ands_22_out_34[26]), .out_51(n32ands_22_out_34[27]),
    .out_52(n32ands_22_out_34[28]), .out_53(n32ands_22_out_34[29]), .out_54(n32ands_22_out_34[30]),
    .out_55(n32ands_22_out_34[31]), .in_1(B10));  // open: out_56, out_57, out_58, out_59, out_60, out_61, out_62, out_63, out_64, out_65
  _32ANDs u_32ands_23 (
    .in_2(A0), .in_3(A1), .in_4(A2), .in_5(A3), .in_6(A4), .in_7(A5), .in_8(A6), .in_9(A7), .in_10(A8),
    .in_11(A9), .in_12(A10), .in_13(A11), .in_14(A12), .in_15(A13), .in_16(A14), .in_17(A15), .in_18(A16),
    .in_19(A17), .in_20(A18), .in_21(A19), .in_22(A20), .in_23(A21), .in_24(A22), .in_25(A23), .in_26(A24),
    .in_27(A25), .in_28(A26), .in_29(A27), .in_30(A28), .in_31(A29), .in_32(A30), .in_33(1'b0),
    .out_34(n32ands_23_out_34[9]), .out_35(n32ands_23_out_34[10]), .out_36(n32ands_23_out_34[11]),
    .out_37(n32ands_23_out_34[12]), .out_38(n32ands_23_out_34[13]), .out_39(n32ands_23_out_34[14]),
    .out_40(n32ands_23_out_34[15]), .out_41(n32ands_23_out_34[16]), .out_42(n32ands_23_out_34[17]),
    .out_43(n32ands_23_out_34[18]), .out_44(n32ands_23_out_34[19]), .out_45(n32ands_23_out_34[20]),
    .out_46(n32ands_23_out_34[21]), .out_47(n32ands_23_out_34[22]), .out_48(n32ands_23_out_34[23]),
    .out_49(n32ands_23_out_34[24]), .out_50(n32ands_23_out_34[25]), .out_51(n32ands_23_out_34[26]),
    .out_52(n32ands_23_out_34[27]), .out_53(n32ands_23_out_34[28]), .out_54(n32ands_23_out_34[29]),
    .out_55(n32ands_23_out_34[30]), .out_56(n32ands_23_out_34[31]), .in_1(B9));  // open: out_57, out_58, out_59, out_60, out_61, out_62, out_63, out_64, out_65
  _32ANDs u_32ands_24 (
    .in_2(A0), .in_3(A1), .in_4(A2), .in_5(A3), .in_6(A4), .in_7(A5), .in_8(A6), .in_9(A7), .in_10(A8),
    .in_11(A9), .in_12(A10), .in_13(A11), .in_14(A12), .in_15(A13), .in_16(A14), .in_17(A15), .in_18(A16),
    .in_19(A17), .in_20(A18), .in_21(A19), .in_22(A20), .in_23(A21), .in_24(A22), .in_25(A23), .in_26(A24),
    .in_27(A25), .in_28(A26), .in_29(A27), .in_30(A28), .in_31(A29), .in_32(A30), .in_33(1'b0),
    .out_34(n32ands_24_out_34[8]), .out_35(n32ands_24_out_34[9]), .out_36(n32ands_24_out_34[10]),
    .out_37(n32ands_24_out_34[11]), .out_38(n32ands_24_out_34[12]), .out_39(n32ands_24_out_34[13]),
    .out_40(n32ands_24_out_34[14]), .out_41(n32ands_24_out_34[15]), .out_42(n32ands_24_out_34[16]),
    .out_43(n32ands_24_out_34[17]), .out_44(n32ands_24_out_34[18]), .out_45(n32ands_24_out_34[19]),
    .out_46(n32ands_24_out_34[20]), .out_47(n32ands_24_out_34[21]), .out_48(n32ands_24_out_34[22]),
    .out_49(n32ands_24_out_34[23]), .out_50(n32ands_24_out_34[24]), .out_51(n32ands_24_out_34[25]),
    .out_52(n32ands_24_out_34[26]), .out_53(n32ands_24_out_34[27]), .out_54(n32ands_24_out_34[28]),
    .out_55(n32ands_24_out_34[29]), .out_56(n32ands_24_out_34[30]), .out_57(n32ands_24_out_34[31]), .in_1(B8));  // open: out_58, out_59, out_60, out_61, out_62, out_63, out_64, out_65
  _32ANDs u_32ands_25 (
    .in_2(A0), .in_3(A1), .in_4(A2), .in_5(A3), .in_6(A4), .in_7(A5), .in_8(A6), .in_9(A7), .in_10(A8),
    .in_11(A9), .in_12(A10), .in_13(A11), .in_14(A12), .in_15(A13), .in_16(A14), .in_17(A15), .in_18(A16),
    .in_19(A17), .in_20(A18), .in_21(A19), .in_22(A20), .in_23(A21), .in_24(A22), .in_25(A23), .in_26(A24),
    .in_27(A25), .in_28(A26), .in_29(A27), .in_30(A28), .in_31(A29), .in_32(A30), .in_33(1'b0),
    .out_34(n32ands_25_out_34[7]), .out_35(n32ands_25_out_34[8]), .out_36(n32ands_25_out_34[9]),
    .out_37(n32ands_25_out_34[10]), .out_38(n32ands_25_out_34[11]), .out_39(n32ands_25_out_34[12]),
    .out_40(n32ands_25_out_34[13]), .out_41(n32ands_25_out_34[14]), .out_42(n32ands_25_out_34[15]),
    .out_43(n32ands_25_out_34[16]), .out_44(n32ands_25_out_34[17]), .out_45(n32ands_25_out_34[18]),
    .out_46(n32ands_25_out_34[19]), .out_47(n32ands_25_out_34[20]), .out_48(n32ands_25_out_34[21]),
    .out_49(n32ands_25_out_34[22]), .out_50(n32ands_25_out_34[23]), .out_51(n32ands_25_out_34[24]),
    .out_52(n32ands_25_out_34[25]), .out_53(n32ands_25_out_34[26]), .out_54(n32ands_25_out_34[27]),
    .out_55(n32ands_25_out_34[28]), .out_56(n32ands_25_out_34[29]), .out_57(n32ands_25_out_34[30]),
    .out_58(n32ands_25_out_34[31]), .in_1(B7));  // open: out_59, out_60, out_61, out_62, out_63, out_64, out_65
  _32ANDs u_32ands_26 (
    .in_2(A0), .in_3(A1), .in_4(A2), .in_5(A3), .in_6(A4), .in_7(A5), .in_8(A6), .in_9(A7), .in_10(A8),
    .in_11(A9), .in_12(A10), .in_13(A11), .in_14(A12), .in_15(A13), .in_16(A14), .in_17(A15), .in_18(A16),
    .in_19(A17), .in_20(A18), .in_21(A19), .in_22(A20), .in_23(A21), .in_24(A22), .in_25(A23), .in_26(A24),
    .in_27(A25), .in_28(A26), .in_29(A27), .in_30(A28), .in_31(A29), .in_32(A30), .in_33(1'b0),
    .out_34(n32ands_26_out_34[6]), .out_35(n32ands_26_out_34[7]), .out_36(n32ands_26_out_34[8]),
    .out_37(n32ands_26_out_34[9]), .out_38(n32ands_26_out_34[10]), .out_39(n32ands_26_out_34[11]),
    .out_40(n32ands_26_out_34[12]), .out_41(n32ands_26_out_34[13]), .out_42(n32ands_26_out_34[14]),
    .out_43(n32ands_26_out_34[15]), .out_44(n32ands_26_out_34[16]), .out_45(n32ands_26_out_34[17]),
    .out_46(n32ands_26_out_34[18]), .out_47(n32ands_26_out_34[19]), .out_48(n32ands_26_out_34[20]),
    .out_49(n32ands_26_out_34[21]), .out_50(n32ands_26_out_34[22]), .out_51(n32ands_26_out_34[23]),
    .out_52(n32ands_26_out_34[24]), .out_53(n32ands_26_out_34[25]), .out_54(n32ands_26_out_34[26]),
    .out_55(n32ands_26_out_34[27]), .out_56(n32ands_26_out_34[28]), .out_57(n32ands_26_out_34[29]),
    .out_58(n32ands_26_out_34[30]), .out_59(n32ands_26_out_34[31]), .in_1(B6));  // open: out_60, out_61, out_62, out_63, out_64, out_65
  _32ANDs u_32ands_27 (
    .in_2(A0), .in_3(A1), .in_4(A2), .in_5(A3), .in_6(A4), .in_7(A5), .in_8(A6), .in_9(A7), .in_10(A8),
    .in_11(A9), .in_12(A10), .in_13(A11), .in_14(A12), .in_15(A13), .in_16(A14), .in_17(A15), .in_18(A16),
    .in_19(A17), .in_20(A18), .in_21(A19), .in_22(A20), .in_23(A21), .in_24(A22), .in_25(A23), .in_26(A24),
    .in_27(A25), .in_28(A26), .in_29(A27), .in_30(A28), .in_31(A29), .in_32(A30), .in_33(1'b0),
    .out_34(n32ands_27_out_34[5]), .out_35(n32ands_27_out_34[6]), .out_36(n32ands_27_out_34[7]),
    .out_37(n32ands_27_out_34[8]), .out_38(n32ands_27_out_34[9]), .out_39(n32ands_27_out_34[10]),
    .out_40(n32ands_27_out_34[11]), .out_41(n32ands_27_out_34[12]), .out_42(n32ands_27_out_34[13]),
    .out_43(n32ands_27_out_34[14]), .out_44(n32ands_27_out_34[15]), .out_45(n32ands_27_out_34[16]),
    .out_46(n32ands_27_out_34[17]), .out_47(n32ands_27_out_34[18]), .out_48(n32ands_27_out_34[19]),
    .out_49(n32ands_27_out_34[20]), .out_50(n32ands_27_out_34[21]), .out_51(n32ands_27_out_34[22]),
    .out_52(n32ands_27_out_34[23]), .out_53(n32ands_27_out_34[24]), .out_54(n32ands_27_out_34[25]),
    .out_55(n32ands_27_out_34[26]), .out_56(n32ands_27_out_34[27]), .out_57(n32ands_27_out_34[28]),
    .out_58(n32ands_27_out_34[29]), .out_59(n32ands_27_out_34[30]), .out_60(n32ands_27_out_34[31]), .in_1(B5));  // open: out_61, out_62, out_63, out_64, out_65
  _32ANDs u_32ands_28 (
    .in_2(A0), .in_3(A1), .in_4(A2), .in_5(A3), .in_6(A4), .in_7(A5), .in_8(A6), .in_9(A7), .in_10(A8),
    .in_11(A9), .in_12(A10), .in_13(A11), .in_14(A12), .in_15(A13), .in_16(A14), .in_17(A15), .in_18(A16),
    .in_19(A17), .in_20(A18), .in_21(A19), .in_22(A20), .in_23(A21), .in_24(A22), .in_25(A23), .in_26(A24),
    .in_27(A25), .in_28(A26), .in_29(A27), .in_30(A28), .in_31(A29), .in_32(A30), .in_33(1'b0),
    .out_34(n32ands_28_out_34[4]), .out_35(n32ands_28_out_34[5]), .out_36(n32ands_28_out_34[6]),
    .out_37(n32ands_28_out_34[7]), .out_38(n32ands_28_out_34[8]), .out_39(n32ands_28_out_34[9]),
    .out_40(n32ands_28_out_34[10]), .out_41(n32ands_28_out_34[11]), .out_42(n32ands_28_out_34[12]),
    .out_43(n32ands_28_out_34[13]), .out_44(n32ands_28_out_34[14]), .out_45(n32ands_28_out_34[15]),
    .out_46(n32ands_28_out_34[16]), .out_47(n32ands_28_out_34[17]), .out_48(n32ands_28_out_34[18]),
    .out_49(n32ands_28_out_34[19]), .out_50(n32ands_28_out_34[20]), .out_51(n32ands_28_out_34[21]),
    .out_52(n32ands_28_out_34[22]), .out_53(n32ands_28_out_34[23]), .out_54(n32ands_28_out_34[24]),
    .out_55(n32ands_28_out_34[25]), .out_56(n32ands_28_out_34[26]), .out_57(n32ands_28_out_34[27]),
    .out_58(n32ands_28_out_34[28]), .out_59(n32ands_28_out_34[29]), .out_60(n32ands_28_out_34[30]),
    .out_61(n32ands_28_out_34[31]), .in_1(B4));  // open: out_62, out_63, out_64, out_65
  _32ANDs u_32ands_29 (
    .in_2(A0), .in_3(A1), .in_4(A2), .in_5(A3), .in_6(A4), .in_7(A5), .in_8(A6), .in_9(A7), .in_10(A8),
    .in_11(A9), .in_12(A10), .in_13(A11), .in_14(A12), .in_15(A13), .in_16(A14), .in_17(A15), .in_18(A16),
    .in_19(A17), .in_20(A18), .in_21(A19), .in_22(A20), .in_23(A21), .in_24(A22), .in_25(A23), .in_26(A24),
    .in_27(A25), .in_28(A26), .in_29(A27), .in_30(A28), .in_31(A29), .in_32(A30), .in_33(1'b0),
    .out_34(n32ands_29_out_34[3]), .out_35(n32ands_29_out_34[4]), .out_36(n32ands_29_out_34[5]),
    .out_37(n32ands_29_out_34[6]), .out_38(n32ands_29_out_34[7]), .out_39(n32ands_29_out_34[8]),
    .out_40(n32ands_29_out_34[9]), .out_41(n32ands_29_out_34[10]), .out_42(n32ands_29_out_34[11]),
    .out_43(n32ands_29_out_34[12]), .out_44(n32ands_29_out_34[13]), .out_45(n32ands_29_out_34[14]),
    .out_46(n32ands_29_out_34[15]), .out_47(n32ands_29_out_34[16]), .out_48(n32ands_29_out_34[17]),
    .out_49(n32ands_29_out_34[18]), .out_50(n32ands_29_out_34[19]), .out_51(n32ands_29_out_34[20]),
    .out_52(n32ands_29_out_34[21]), .out_53(n32ands_29_out_34[22]), .out_54(n32ands_29_out_34[23]),
    .out_55(n32ands_29_out_34[24]), .out_56(n32ands_29_out_34[25]), .out_57(n32ands_29_out_34[26]),
    .out_58(n32ands_29_out_34[27]), .out_59(n32ands_29_out_34[28]), .out_60(n32ands_29_out_34[29]),
    .out_61(n32ands_29_out_34[30]), .out_62(n32ands_29_out_34[31]), .in_1(B3));  // open: out_63, out_64, out_65
  _32ANDs u_32ands_30 (
    .in_2(A0), .in_3(A1), .in_4(A2), .in_5(A3), .in_6(A4), .in_7(A5), .in_8(A6), .in_9(A7), .in_10(A8),
    .in_11(A9), .in_12(A10), .in_13(A11), .in_14(A12), .in_15(A13), .in_16(A14), .in_17(A15), .in_18(A16),
    .in_19(A17), .in_20(A18), .in_21(A19), .in_22(A20), .in_23(A21), .in_24(A22), .in_25(A23), .in_26(A24),
    .in_27(A25), .in_28(A26), .in_29(A27), .in_30(A28), .in_31(A29), .in_32(A30), .in_33(1'b0),
    .out_34(n32ands_30_out_34[2]), .out_35(n32ands_30_out_34[3]), .out_36(n32ands_30_out_34[4]),
    .out_37(n32ands_30_out_34[5]), .out_38(n32ands_30_out_34[6]), .out_39(n32ands_30_out_34[7]),
    .out_40(n32ands_30_out_34[8]), .out_41(n32ands_30_out_34[9]), .out_42(n32ands_30_out_34[10]),
    .out_43(n32ands_30_out_34[11]), .out_44(n32ands_30_out_34[12]), .out_45(n32ands_30_out_34[13]),
    .out_46(n32ands_30_out_34[14]), .out_47(n32ands_30_out_34[15]), .out_48(n32ands_30_out_34[16]),
    .out_49(n32ands_30_out_34[17]), .out_50(n32ands_30_out_34[18]), .out_51(n32ands_30_out_34[19]),
    .out_52(n32ands_30_out_34[20]), .out_53(n32ands_30_out_34[21]), .out_54(n32ands_30_out_34[22]),
    .out_55(n32ands_30_out_34[23]), .out_56(n32ands_30_out_34[24]), .out_57(n32ands_30_out_34[25]),
    .out_58(n32ands_30_out_34[26]), .out_59(n32ands_30_out_34[27]), .out_60(n32ands_30_out_34[28]),
    .out_61(n32ands_30_out_34[29]), .out_62(n32ands_30_out_34[30]), .out_63(n32ands_30_out_34[31]), .in_1(B2));  // open: out_64, out_65
  _32ANDs u_32ands_31 (
    .in_2(A0), .in_3(A1), .in_4(A2), .in_5(A3), .in_6(A4), .in_7(A5), .in_8(A6), .in_9(A7), .in_10(A8),
    .in_11(A9), .in_12(A10), .in_13(A11), .in_14(A12), .in_15(A13), .in_16(A14), .in_17(A15), .in_18(A16),
    .in_19(A17), .in_20(A18), .in_21(A19), .in_22(A20), .in_23(A21), .in_24(A22), .in_25(A23), .in_26(A24),
    .in_27(A25), .in_28(A26), .in_29(A27), .in_30(A28), .in_31(A29), .in_32(A30), .in_33(1'b0),
    .out_34(n32ands_31_out_34[1]), .out_35(n32ands_31_out_34[2]), .out_36(n32ands_31_out_34[3]),
    .out_37(n32ands_31_out_34[4]), .out_38(n32ands_31_out_34[5]), .out_39(n32ands_31_out_34[6]),
    .out_40(n32ands_31_out_34[7]), .out_41(n32ands_31_out_34[8]), .out_42(n32ands_31_out_34[9]),
    .out_43(n32ands_31_out_34[10]), .out_44(n32ands_31_out_34[11]), .out_45(n32ands_31_out_34[12]),
    .out_46(n32ands_31_out_34[13]), .out_47(n32ands_31_out_34[14]), .out_48(n32ands_31_out_34[15]),
    .out_49(n32ands_31_out_34[16]), .out_50(n32ands_31_out_34[17]), .out_51(n32ands_31_out_34[18]),
    .out_52(n32ands_31_out_34[19]), .out_53(n32ands_31_out_34[20]), .out_54(n32ands_31_out_34[21]),
    .out_55(n32ands_31_out_34[22]), .out_56(n32ands_31_out_34[23]), .out_57(n32ands_31_out_34[24]),
    .out_58(n32ands_31_out_34[25]), .out_59(n32ands_31_out_34[26]), .out_60(n32ands_31_out_34[27]),
    .out_61(n32ands_31_out_34[28]), .out_62(n32ands_31_out_34[29]), .out_63(n32ands_31_out_34[30]),
    .out_64(n32ands_31_out_34[31]), .in_1(B1));  // open: out_65
  _32ANDs u_32ands_32 (
    .in_2(A0), .in_3(A1), .in_4(A2), .in_5(A3), .in_6(A4), .in_7(A5), .in_8(A6), .in_9(A7), .in_10(A8),
    .in_11(A9), .in_12(A10), .in_13(A11), .in_14(A12), .in_15(A13), .in_16(A14), .in_17(A15), .in_18(A16),
    .in_19(A17), .in_20(A18), .in_21(A19), .in_22(A20), .in_23(A21), .in_24(A22), .in_25(A23), .in_26(A24),
    .in_27(A25), .in_28(A26), .in_29(A27), .in_30(A28), .in_31(A29), .in_32(A30), .in_33(1'b0),
    .out_34(n32ands_32_out_34[0]), .out_35(n32ands_32_out_34[1]), .out_36(n32ands_32_out_34[2]),
    .out_37(n32ands_32_out_34[3]), .out_38(n32ands_32_out_34[4]), .out_39(n32ands_32_out_34[5]),
    .out_40(n32ands_32_out_34[6]), .out_41(n32ands_32_out_34[7]), .out_42(n32ands_32_out_34[8]),
    .out_43(n32ands_32_out_34[9]), .out_44(n32ands_32_out_34[10]), .out_45(n32ands_32_out_34[11]),
    .out_46(n32ands_32_out_34[12]), .out_47(n32ands_32_out_34[13]), .out_48(n32ands_32_out_34[14]),
    .out_49(n32ands_32_out_34[15]), .out_50(n32ands_32_out_34[16]), .out_51(n32ands_32_out_34[17]),
    .out_52(n32ands_32_out_34[18]), .out_53(n32ands_32_out_34[19]), .out_54(n32ands_32_out_34[20]),
    .out_55(n32ands_32_out_34[21]), .out_56(n32ands_32_out_34[22]), .out_57(n32ands_32_out_34[23]),
    .out_58(n32ands_32_out_34[24]), .out_59(n32ands_32_out_34[25]), .out_60(n32ands_32_out_34[26]),
    .out_61(n32ands_32_out_34[27]), .out_62(n32ands_32_out_34[28]), .out_63(n32ands_32_out_34[29]),
    .out_64(n32ands_32_out_34[30]), .out_65(n32ands_32_out_34[31]), .in_1(B0));
  Soma_de_32_bits soma_de_32_bits_1 (
    .A({n32ands_1_out_34[31], {31{1'b0}}}), .B({n32ands_2_out_34, {30{1'b0}}}), .S(soma_de_32_bits_1_s),
    .Cin(1'b0), .Cout(soma_de_32_bits_1_cout));
  Soma_de_32_bits soma_de_32_bits_2 (
    .A({n32ands_3_out_34, {29{1'b0}}}), .B({n32ands_4_out_34, {28{1'b0}}}), .S(soma_de_32_bits_2_s),
    .Cin(soma_de_32_bits_1_cout), .Cout(soma_de_32_bits_2_cout));
  Soma_de_32_bits soma_de_32_bits_3 (
    .A({n32ands_5_out_34, {27{1'b0}}}), .B({n32ands_6_out_34, {26{1'b0}}}), .S(soma_de_32_bits_3_s),
    .Cin(soma_de_32_bits_2_cout), .Cout(soma_de_32_bits_3_cout));
  Soma_de_32_bits soma_de_32_bits_4 (
    .A({n32ands_7_out_34, {25{1'b0}}}), .B({n32ands_8_out_34, {24{1'b0}}}), .S(soma_de_32_bits_4_s),
    .Cin(soma_de_32_bits_3_cout), .Cout(soma_de_32_bits_4_cout));
  Soma_de_32_bits soma_de_32_bits_5 (
    .A({n32ands_9_out_34, {23{1'b0}}}), .B({n32ands_10_out_34, {22{1'b0}}}), .S(soma_de_32_bits_5_s),
    .Cin(soma_de_32_bits_4_cout), .Cout(soma_de_32_bits_5_cout));
  Soma_de_32_bits soma_de_32_bits_6 (
    .A({n32ands_11_out_34, {21{1'b0}}}), .B({n32ands_12_out_34, {20{1'b0}}}), .S(soma_de_32_bits_6_s),
    .Cin(soma_de_32_bits_5_cout), .Cout(soma_de_32_bits_6_cout));
  Soma_de_32_bits soma_de_32_bits_7 (
    .A({n32ands_13_out_34, {19{1'b0}}}), .B({n32ands_14_out_34, {18{1'b0}}}), .S(soma_de_32_bits_7_s),
    .Cin(soma_de_32_bits_6_cout), .Cout(soma_de_32_bits_7_cout));
  Soma_de_32_bits soma_de_32_bits_8 (
    .A({n32ands_15_out_34, {17{1'b0}}}), .B({n32ands_16_out_34, {16{1'b0}}}), .S(soma_de_32_bits_8_s),
    .Cin(soma_de_32_bits_7_cout), .Cout(soma_de_32_bits_8_cout));
  Soma_de_32_bits soma_de_32_bits_9 (
    .A({n32ands_17_out_34, {15{1'b0}}}), .B({n32ands_18_out_34, {14{1'b0}}}), .S(soma_de_32_bits_9_s),
    .Cin(soma_de_32_bits_8_cout), .Cout(soma_de_32_bits_9_cout));
  Soma_de_32_bits soma_de_32_bits_10 (
    .A({n32ands_19_out_34, {13{1'b0}}}), .B({n32ands_20_out_34, {12{1'b0}}}), .S(soma_de_32_bits_10_s),
    .Cin(soma_de_32_bits_9_cout), .Cout(soma_de_32_bits_10_cout));
  Soma_de_32_bits soma_de_32_bits_11 (
    .A({n32ands_21_out_34, {11{1'b0}}}), .B({n32ands_22_out_34, {10{1'b0}}}), .S(soma_de_32_bits_11_s),
    .Cin(soma_de_32_bits_10_cout), .Cout(soma_de_32_bits_11_cout));
  Soma_de_32_bits soma_de_32_bits_12 (
    .A({n32ands_23_out_34, {9{1'b0}}}), .B({n32ands_24_out_34, {8{1'b0}}}), .S(soma_de_32_bits_12_s),
    .Cin(soma_de_32_bits_11_cout), .Cout(soma_de_32_bits_12_cout));
  Soma_de_32_bits soma_de_32_bits_13 (
    .A({n32ands_25_out_34, {7{1'b0}}}), .B({n32ands_26_out_34, {6{1'b0}}}), .S(soma_de_32_bits_13_s),
    .Cin(soma_de_32_bits_12_cout), .Cout(soma_de_32_bits_13_cout));
  Soma_de_32_bits soma_de_32_bits_14 (
    .A({n32ands_27_out_34, {5{1'b0}}}), .B({n32ands_28_out_34, 4'b0000}), .S(soma_de_32_bits_14_s),
    .Cin(soma_de_32_bits_13_cout), .Cout(soma_de_32_bits_14_cout));
  Soma_de_32_bits soma_de_32_bits_15 (
    .A({n32ands_29_out_34, 3'b000}), .B({n32ands_30_out_34, 2'b00}), .S(soma_de_32_bits_15_s),
    .Cin(soma_de_32_bits_14_cout), .Cout(soma_de_32_bits_15_cout));
  Soma_de_32_bits soma_de_32_bits_16 (
    .A({n32ands_31_out_34, 1'b0}), .B(n32ands_32_out_34), .S(soma_de_32_bits_16_s),
    .Cin(soma_de_32_bits_15_cout), .Cout(soma_de_32_bits_16_cout));
  Soma_de_32_bits soma_de_32_bits_17 (
    .A(soma_de_32_bits_1_s), .B(soma_de_32_bits_2_s), .S(soma_de_32_bits_17_s), .Cin(1'b0),
    .Cout(soma_de_32_bits_17_cout));
  Soma_de_32_bits soma_de_32_bits_18 (
    .A(soma_de_32_bits_3_s), .B(soma_de_32_bits_4_s), .S(soma_de_32_bits_18_s),
    .Cin(soma_de_32_bits_17_cout), .Cout(soma_de_32_bits_18_cout));
  Soma_de_32_bits soma_de_32_bits_19 (
    .A(soma_de_32_bits_5_s), .B(soma_de_32_bits_6_s), .S(soma_de_32_bits_19_s),
    .Cin(soma_de_32_bits_18_cout), .Cout(soma_de_32_bits_19_cout));
  Soma_de_32_bits soma_de_32_bits_20 (
    .A(soma_de_32_bits_7_s), .B(soma_de_32_bits_8_s), .S(soma_de_32_bits_20_s),
    .Cin(soma_de_32_bits_19_cout), .Cout(soma_de_32_bits_20_cout));
  Soma_de_32_bits soma_de_32_bits_21 (
    .A(soma_de_32_bits_9_s), .B(soma_de_32_bits_10_s), .S(soma_de_32_bits_21_s),
    .Cin(soma_de_32_bits_20_cout), .Cout(soma_de_32_bits_21_cout));
  Soma_de_32_bits soma_de_32_bits_22 (
    .A(soma_de_32_bits_11_s), .B(soma_de_32_bits_12_s), .S(soma_de_32_bits_22_s),
    .Cin(soma_de_32_bits_21_cout), .Cout(soma_de_32_bits_22_cout));
  Soma_de_32_bits soma_de_32_bits_23 (
    .A(soma_de_32_bits_13_s), .B(soma_de_32_bits_14_s), .S(soma_de_32_bits_23_s),
    .Cin(soma_de_32_bits_22_cout), .Cout(soma_de_32_bits_23_cout));
  Soma_de_32_bits soma_de_32_bits_24 (
    .A(soma_de_32_bits_15_s), .B(soma_de_32_bits_16_s), .S(soma_de_32_bits_24_s),
    .Cin(soma_de_32_bits_23_cout), .Cout(soma_de_32_bits_24_cout));
  Soma_de_32_bits soma_de_32_bits_25 (
    .A(soma_de_32_bits_17_s), .B(soma_de_32_bits_18_s), .S(soma_de_32_bits_25_s), .Cin(1'b0),
    .Cout(soma_de_32_bits_25_cout));
  Soma_de_32_bits soma_de_32_bits_26 (
    .A(soma_de_32_bits_19_s), .B(soma_de_32_bits_20_s), .S(soma_de_32_bits_26_s),
    .Cin(soma_de_32_bits_25_cout), .Cout(soma_de_32_bits_26_cout));
  Soma_de_32_bits soma_de_32_bits_27 (
    .A(soma_de_32_bits_21_s), .B(soma_de_32_bits_22_s), .S(soma_de_32_bits_27_s),
    .Cin(soma_de_32_bits_26_cout), .Cout(soma_de_32_bits_27_cout));
  Soma_de_32_bits soma_de_32_bits_28 (
    .A(soma_de_32_bits_23_s), .B(soma_de_32_bits_24_s), .S(soma_de_32_bits_28_s),
    .Cin(soma_de_32_bits_27_cout), .Cout(soma_de_32_bits_28_cout));
  Soma_de_32_bits soma_de_32_bits_29 (
    .A(soma_de_32_bits_25_s), .B(soma_de_32_bits_26_s), .S(soma_de_32_bits_29_s), .Cin(1'b0),
    .Cout(soma_de_32_bits_29_cout));
  Soma_de_32_bits soma_de_32_bits_30 (
    .A(soma_de_32_bits_27_s), .B(soma_de_32_bits_28_s), .S(soma_de_32_bits_30_s),
    .Cin(soma_de_32_bits_29_cout), .Cout(soma_de_32_bits_30_cout));
  Soma_de_32_bits soma_de_32_bits_31 (
    .A(soma_de_32_bits_29_s), .B(soma_de_32_bits_30_s),
    .S({soma_de_32_bits_31_s[31], S30, S29, S28, S27, S26, S25, S24, S23, S22, S21, S20, S19, S18, S17, S16, S15, S14, S13, S12, S11, S10, S9, S8, S7, S6, S5, S4, S3, S2, S1, S0}),
    .Cin(1'b0), .Cout(soma_de_32_bits_31_cout));
  xor xor_1 (S31, A31, B31);
  // also tied to GND on the sheet: {soma_de_32_bits_16_cout, soma_de_32_bits_24_cout, soma_de_32_bits_28_cout, soma_de_32_bits_30_cout, soma_de_32_bits_31_cout}
endmodule

module _32ANDs (
  input  in_1,
  input  in_2,
  input  in_3,
  input  in_4,
  input  in_5,
  input  in_6,
  input  in_7,
  input  in_8,
  input  in_9,
  input  in_10,
  input  in_11,
  input  in_12,
  input  in_13,
  input  in_14,
  input  in_15,
  input  in_16,
  input  in_17,
  input  in_18,
  input  in_19,
  input  in_20,
  input  in_21,
  input  in_22,
  input  in_23,
  input  in_24,
  input  in_25,
  input  in_26,
  input  in_27,
  input  in_28,
  input  in_29,
  input  in_30,
  input  in_31,
  input  in_32,
  input  in_33,
  output out_34,
  output out_35,
  output out_36,
  output out_37,
  output out_38,
  output out_39,
  output out_40,
  output out_41,
  output out_42,
  output out_43,
  output out_44,
  output out_45,
  output out_46,
  output out_47,
  output out_48,
  output out_49,
  output out_50,
  output out_51,
  output out_52,
  output out_53,
  output out_54,
  output out_55,
  output out_56,
  output out_57,
  output out_58,
  output out_59,
  output out_60,
  output out_61,
  output out_62,
  output out_63,
  output out_64,
  output out_65
);

  and and_1 (out_34, in_2, in_1);
  and and_2 (out_35, in_3, in_1);
  and and_3 (out_36, in_4, in_1);
  and and_4 (out_37, in_5, in_1);
  and and_5 (out_38, in_6, in_1);
  and and_6 (out_39, in_7, in_1);
  and and_7 (out_40, in_8, in_1);
  and and_8 (out_41, in_9, in_1);
  and and_9 (out_42, in_10, in_1);
  and and_10 (out_43, in_11, in_1);
  and and_11 (out_44, in_12, in_1);
  and and_12 (out_45, in_13, in_1);
  and and_13 (out_46, in_14, in_1);
  and and_14 (out_47, in_15, in_1);
  and and_15 (out_48, in_16, in_1);
  and and_16 (out_49, in_17, in_1);
  and and_17 (out_50, in_18, in_1);
  and and_18 (out_51, in_19, in_1);
  and and_19 (out_52, in_20, in_1);
  and and_20 (out_53, in_21, in_1);
  and and_21 (out_54, in_22, in_1);
  and and_22 (out_55, in_23, in_1);
  and and_23 (out_56, in_24, in_1);
  and and_24 (out_57, in_25, in_1);
  and and_25 (out_58, in_26, in_1);
  and and_26 (out_59, in_27, in_1);
  and and_27 (out_60, in_28, in_1);
  and and_28 (out_61, in_29, in_1);
  and and_29 (out_62, in_30, in_1);
  and and_30 (out_63, in_31, in_1);
  and and_31 (out_64, in_32, in_1);
  and and_32 (out_65, in_33, in_1);
endmodule

module Soma_de_32_bits (
  input  Cin,
  input  [31:0] A,
  input  [31:0] B,
  output [31:0] S,
  output Cout
);

  wire soma_de_16_bits_1_cout;

  Soma_de_16_bits soma_de_16_bits_1 (.A(A[15:0]), .B(B[15:0]), .S(S[15:0]), .Cin(Cin), .Cout(soma_de_16_bits_1_cout));
  Soma_de_16_bits soma_de_16_bits_2 (
    .A(A[31:16]), .B(B[31:16]), .S(S[31:16]), .Cin(soma_de_16_bits_1_cout), .Cout(Cout));
endmodule

module Soma_de_1_bit (
  input  Cin,
  input  A,
  input  B,
  output S,
  output Cout
);

  wire and_1_out, and_2_out, xor_1_out;

  xor xor_1 (xor_1_out, A, B);
  xor xor_2 (S, xor_1_out, Cin);
  and and_1 (and_1_out, xor_1_out, Cin);
  and and_2 (and_2_out, A, B);
  or or_1 (Cout, and_1_out, and_2_out);
endmodule

module Soma_de_2_bits (
  input  Cin,
  input  [1:0] A,
  input  [1:0] B,
  output [1:0] out_4,
  output Cout
);

  wire soma_de_1_bit_1_cout;

  Soma_de_1_bit soma_de_1_bit_1 (.A(A[0]), .B(B[0]), .S(out_4[0]), .Cin(Cin), .Cout(soma_de_1_bit_1_cout));
  Soma_de_1_bit soma_de_1_bit_2 (.A(A[1]), .B(B[1]), .S(out_4[1]), .Cin(soma_de_1_bit_1_cout), .Cout(Cout));
endmodule

module Soma_de_4_bits (
  input  Cin,
  input  [3:0] A,
  input  [3:0] B,
  output [3:0] S,
  output Cout
);

  wire soma_de_2_bits_1_cout;

  Soma_de_2_bits soma_de_2_bits_1 (.A(A[1:0]), .B(B[1:0]), .out_4(S[1:0]), .Cin(Cin), .Cout(soma_de_2_bits_1_cout));
  Soma_de_2_bits soma_de_2_bits_2 (.A(A[3:2]), .B(B[3:2]), .out_4(S[3:2]), .Cin(soma_de_2_bits_1_cout), .Cout(Cout));
endmodule

module Soma_de_8_bits (
  input  Cin,
  input  [7:0] A,
  input  [7:0] B,
  output [7:0] S,
  output Cout
);

  wire soma_de_4_bits_1_cout;

  Soma_de_4_bits soma_de_4_bits_1 (.A(A[3:0]), .B(B[3:0]), .S(S[3:0]), .Cin(Cin), .Cout(soma_de_4_bits_1_cout));
  Soma_de_4_bits soma_de_4_bits_2 (.A(A[7:4]), .B(B[7:4]), .S(S[7:4]), .Cin(soma_de_4_bits_1_cout), .Cout(Cout));
endmodule

module Soma_de_16_bits (
  input  Cin,
  input  [15:0] A,
  input  [15:0] B,
  output [15:0] S,
  output Cout
);

  wire soma_de_8_bits_1_cout;

  Soma_de_8_bits soma_de_8_bits_1 (.A(A[7:0]), .B(B[7:0]), .S(S[7:0]), .Cin(Cin), .Cout(soma_de_8_bits_1_cout));
  Soma_de_8_bits soma_de_8_bits_2 (.A(A[15:8]), .B(B[15:8]), .S(S[15:8]), .Cin(soma_de_8_bits_1_cout), .Cout(Cout));
endmodule
